# Fritzing sketch ESP8266WiFiAnalyzer (saved by Fritzing 0.9.3b)
breadboards: 2

parts:
  U1 = 2.4" TFT LCD screen, SPI, Touch-enabled
  U2 = NodeMCU V1.0

nets:
  N1: U1.LED, U2.3V3
  N2: U1.SCL, U2.D5
  N3: U1.SDA, U2.D7
  N4: U1.DC, U2.D1
  N5: U1.RESET, U2.RST
  N6: U1.CS, U2.D8
  GND: U1.GND, U2.GND
  VCC: U1.VCC, U2.Vin

custom parts:
  2.4" TFT LCD screen, SPI, Touch-enabled: 2.4", ILI9341-based TFT LCD screen with touch-sensing using the XPT2046 controller, SPI-compatible. There is also an SD-card version that is non-touch enabled but uses exactly the same board and pinout. This part is for both, though it should be noted that the SD reader and the touch screen are mutually incompatible
  NodeMCU V1.0: ESP8266 based NodeMCU
