# Fritzing sketch PortableWiFiAnalyzer (saved by Fritzing 0.9.3b)

parts:
  U1 = 2.4" TFT LCD screen, SPI, Touch-enabled
  U4 = ESP8266 WiFi Module [part_number=ESP8266]
  Q1 = PNP-Transistor [package="TO92 [THT]"]
  R1 = Resistor [tolerance=±5% resistance=10k package=THT]
  Part1 = PowerBoost 500 Charger
  U5 = LIPO-1000mAh [package=lipo-1000]
  IC1 = Voltage Regulator [package=to-92]
  R2 = Resistor [tolerance=±5% resistance=10k package=THT]
  C2 = Capacitor [package=cap-pth-small2]
  R3 = Resistor [tolerance=±5% resistance=10k package=THT]
  C1 = Electrolytic Capacitor [capacitance=100µF package="200 mil [THT, electrolytic]"]
  S1 = Pushbutton [package="[SMD]"]

nets:
  N1: U1.SDO, U4.GPIO_12
  N2: U1.LED, U1.VCC, Q1.E
  N3: U1.SCL, U4.GPIO_14
  N4: U1.SDA, U4.GPIO_13
  N5: U1.DC, U4.GPIO_4
  N6: U1.RESET, U4.REST, S1.Pin_3, S1.Pin_4
  N7: U1.CS, U4.GPIO_2
  GND: U1.GND, U4.GND, Part1.GND, IC1.GND, R2.Pin_0, C2.1, C1.-, S1.Pin_1, S1.Pin_2
  N8: U4.VCC, Q1.C, R1.Pin_0, IC1.OUT, C2.2, C1.+
  N9: U4.CH_PD, R1.Pin_1
  N10: U4.GPIO_15, R2.Pin_1
  N11: U4.GPIO_5, R3.Pin_0
  N12: Q1.B, R3.Pin_1
  N13: Part1.GND_BAT_IN, U5.-
  N14: Part1.VBAT_IN, U5.+
  N15: Part1.VBAT_OUT, IC1.IN

custom parts:
  2.4" TFT LCD screen, SPI, Touch-enabled: 2.4", ILI9341-based TFT LCD screen with touch-sensing using the XPT2046 controller, SPI-compatible. There is also an SD-card version that is non-touch enabled but uses exactly the same board and pinout. This part is for both, though it should be noted that the SD reader and the touch screen are mutually incompatible
  ESP8266 WiFi Module: Generic WiFi Module based on the ESP8266 with onboard PCB antenna and UART communications
